# Fritzing sketch connect (saved by Fritzing 0.9.2b)

parts:
  Raspberry_Pi1 = Raspberry Pi B+
  LED1 = smd LED [color="Red (633nm)" package="0603 [SMD]"]

nets:
  N1: Raspberry_Pi1.GPIO14, LED1.anode
  N2: Raspberry_Pi1.GND, LED1.cathode
