# Fritzing sketch connect (saved by Fritzing 0.9.2b)
breadboards: 1

parts:
  Raspberry_Pi = Raspberry Pi 2
  RGB_LED = Super Flux RGB LED (com. anode)
  S1 = Pushbutton [package="[SMD]"]
  S2 = Pushbutton [package="[SMD]"]
  S3 = Pushbutton [package="[SMD]"]

nets:
  N1: Raspberry_Pi.GPIO21, S1.Pin_3
  N2: Raspberry_Pi.GPIO20, S2.Pin_3
  N3: Raspberry_Pi.GPIO16, S3.Pin_3, S3.Pin_4
  N4: Raspberry_Pi.GND, S1.Pin_1, S1.Pin_2, S2.Pin_1, S2.Pin_2, S3.Pin_1, S3.Pin_2
  N5: Raspberry_Pi.GPIO18, RGB_LED.green_cathode
  N6: Raspberry_Pi.GPIO15, RGB_LED.red_cathode
  N7: Raspberry_Pi.GPIO14, RGB_LED.blue_cathode
  N8: Raspberry_Pi.5V, RGB_LED.common_anode

notes:
  从树莓派上引GND（负极）到面包板上，3个按钮的一端均接到GND上。另一端接到树莓派GPIO口上。这3个GPIO口在程序里设置为输入模式，并且默认拉到高电平。当某个按钮被按下，即联通GND端到GPIO口上，此时从GPIO口取到的状态为低电平。程序侦测到低电平时就认为按钮被按下，从而做你想做的事情。
