# Fritzing sketch connect (saved by Fritzing 0.9.2b)
breadboards: 1

parts:
  Raspberry_Pi = Raspberry Pi 2
  S1 = Pushbutton [package="[SMD]"]
  LED1 = 7-SEGMENT-4DIGIT-YOUNGSUN [package=7-segment-4digit-youngsun-longpads]

nets:
  N1: Raspberry_Pi.GPIO17, S1.Pin_3
  N2: Raspberry_Pi.GPIO10, LED1.D
  N3: Raspberry_Pi.GPIO9, LED1.DIG3
  N4: Raspberry_Pi.GPIO11, LED1.A
  N5: Raspberry_Pi.GPIO5, LED1.DIG1
  N6: Raspberry_Pi.GPIO6, LED1.DIG2
  N7: Raspberry_Pi.GPIO13, LED1.E
  N8: Raspberry_Pi.GPIO19, LED1.APOS-A
  N9: Raspberry_Pi.GPIO26, LED1.G
  N10: Raspberry_Pi.GPIO21, LED1.DP
  N11: Raspberry_Pi.GPIO20, LED1.F
  N12: Raspberry_Pi.GPIO12, LED1.B
  N13: Raspberry_Pi.GND, S1.Pin_1

custom parts:
  7-SEGMENT-4DIGIT-YOUNGSUN: This is a part for the 4-Digit 7-segment LEDs from Young Sun. Different from the Digikey LEDs, all 16 pins are used. The LONGPADS Variant is used for a test jig, but you may like it because there is more pad to solder to. If you are concerned about routing space, the standard works just fine though.
